// Logisim project logisimlib.circ as structural Verilog
module main (
);

  wire button_1_out, clock_1_out, control_alusrc, control_beq, control_bne, control_regdst;
  wire [1:0] IFID_rd1, IFID_rd2_rt;
  wire [2:0] control_aluctl;
  wire [15:0] IDEX_idex_rd1, IDEX_idex_rd2, instrreg_16b_1_ir, instrreg_16b_1_pc, mem_data, mux_2x1_16b_1_o,
       regfile_4x_16b_1_reg1, regfile_4x_16b_1_reg2;

  ROM #(.addrWidth(16), .dataWidth(16)) mem (.addr(instrreg_16b_1_pc), .data(mem_data));
  Button button_1 (.out(button_1_out));
  instrreg_16b instrreg_16b_1 (
    .mem(mem_data), .Clr(button_1_out), .Clk(clock_1_out), .PC(instrreg_16b_1_pc), .IR(instrreg_16b_1_ir));
  Clock clock_1 (.out(clock_1_out));
  pipeline_ifid_16b IFID (
    .Ir(instrreg_16b_1_ir), .Pc(instrreg_16b_1_pc), .RD1(IFID_rd1), .RD2_RT(IFID_rd2_rt));  // open: Clk, Clr, PCPLUS1, IM, OPCODE, RD
  mux_2x1_2b mux_2x1_2b_1 ();  // open: Op, I1, I0, O
  regfile_4x_16b regfile_4x_16b_1 (
    .Rreg2(IFID_rd2_rt), .REG1(regfile_4x_16b_1_reg1), .REG2(regfile_4x_16b_1_reg2));  // open: Clk, d, RegWrite, Wreg, Clr, Rreg1
  ctrl_idex_4b control (
    .REGDST(control_regdst), .ALUSRC(control_alusrc), .BEQ(control_beq), .BNE(control_bne),
    .ALUCTL(control_aluctl));  // open: Op, MEMTOREG, REGWRITE, MEMWRITE
  Bit_Extender bit_extender_1 ();  // open: in, out
  pipeline_idex_16b IDEX (
    .Rd2(regfile_4x_16b_1_reg2), .Aluctl(control_aluctl), .Beq(control_beq), .Bne(control_bne),
    .Regdst(control_regdst), .Alusrc(control_alusrc), .Rd1(regfile_4x_16b_1_reg1), .IDEX_RD2(IDEX_idex_rd2),
    .IDEX_RD1(IDEX_idex_rd1));  // open: Signext, Rt, Rd, PcPlus1, Regwrite, MemWrite, Clr, Clk, IDEX_SIGNEXT, IDEX_RT, IDEX_RD, IDEX_ALUCTL, IDEX_BEQ, IDEX_BNE, IDEX_REGDST, IDEX_PCPLUS1, IDEX_ALUSRC, IDEX_REGWRITE, IDEX_MEMWRITE
  mux_2x1_16b mux_2x1_16b_1 (.I1(IDEX_idex_rd2), .O(mux_2x1_16b_1_o));  // open: I0, Op
  alu_16b ex (.x(IDEX_idex_rd1), .y(mux_2x1_16b_1_o));  // open: Op, O, R, ZERO

  // Notes on the sheet:
  //   contents of mem (hex, n*v repeats v):
  //   0 510f 5207 0 26c0 0 1780 0 3b80 0 bc0 0 4e40 4b40
endmodule

// INSTRREG
module instrreg_16b (
  input  [15:0] mem,
  input  Clr,
  input  Clk,
  output [15:0] PC,
  output [15:0] IR
);

  wire alu_16b_1_o, alu_16b_1_zero;
  wire [15:0] alu_16b_1_r;

  alu_16b alu_16b_1 (.x(PC), .y(16'h1), .Op(3'b010), .O(alu_16b_1_o), .R(alu_16b_1_r), .ZERO(alu_16b_1_zero));
  reg_16b reg_16b_1 (.Clk(Clk), .Clr(Clr), .d(alu_16b_1_r), .Q(PC));
  reg_16b reg_16b_2 (.Clk(Clk), .Clr(Clr), .d(mem), .Q(IR));
  // NoConnect on alu_16b_1_o
  // NoConnect on alu_16b_1_zero
endmodule

module pipeline_ifid_16b (
  input  [15:0] Pc,
  input  [15:0] Ir,
  input  Clk,
  input  Clr,
  output [15:0] PCPLUS1,
  output [3:0] OPCODE,
  output [1:0] RD1,
  output [1:0] RD2_RT,
  output [1:0] RD,
  output [7:0] IM
);

  reg_16b reg_16b_1 (.Clk(Clk), .Clr(Clr), .d(Pc), .Q(PCPLUS1));
  reg_16b reg_16b_2 (.Clk(Clk), .Clr(Clr), .d(Ir), .Q({IM, RD2_RT, RD1, OPCODE}));

  assign RD = IM[1:0];
endmodule

module pipeline_idex_16b (
  input  Regdst,
  input  [2:0] Aluctl,
  input  Beq,
  input  Bne,
  input  [15:0] PcPlus1,
  input  Alusrc,
  input  Regwrite,
  input  MemWrite,
  input  [15:0] Rd1,
  input  [15:0] Rd2,
  input  [15:0] Signext,
  input  [1:0] Rt,
  input  [1:0] Rd,
  input  Clr,
  input  Clk,
  output IDEX_REGDST,
  output [2:0] IDEX_ALUCTL,
  output IDEX_BEQ,
  output IDEX_BNE,
  output [15:0] IDEX_PCPLUS1,
  output IDEX_ALUSRC,
  output IDEX_REGWRITE,
  output IDEX_MEMWRITE,
  output [15:0] IDEX_RD1,
  output [15:0] IDEX_RD2,
  output [15:0] IDEX_SIGNEXT,
  output [1:0] IDEX_RT,
  output [1:0] IDEX_RD
);

  wire d_flip_flop_1_qp, d_flip_flop_2_qp, d_flip_flop_3_qp, d_flip_flop_4_qp, d_flip_flop_5_qp,
       d_flip_flop_6_qp;

  reg_3b reg_3b_1 (.d(Aluctl), .Clr(Clr), .Clk(Clk), .Q(IDEX_ALUCTL));
  reg_16b reg_16b_1 (.Clk(Clk), .Clr(Clr), .d(PcPlus1), .Q(IDEX_PCPLUS1));
  reg_16b reg_16b_2 (.Clk(Clk), .Clr(Clr), .d(Rd1), .Q(IDEX_RD1));
  reg_16b reg_16b_3 (.Clk(Clk), .Clr(Clr), .d(Rd2), .Q(IDEX_RD2));
  reg_16b reg_16b_4 (.Clk(Clk), .Clr(Clr), .d(Signext), .Q(IDEX_SIGNEXT));
  reg_2b reg_2b_1 (.d(Rt), .Clr(Clr), .Clk(Clk), .Q(IDEX_RT));
  reg_2b reg_2b_2 (.d(Rd), .Clr(Clr), .Clk(Clk), .Q(IDEX_RD));
  d_flip_flop d_flip_flop_1 (.Clr(Clr), .Clk(Clk), .d(Regdst), .QP(d_flip_flop_1_qp), .Q(IDEX_REGDST));
  d_flip_flop d_flip_flop_2 (.Clr(Clr), .Clk(Clk), .d(Beq), .QP(d_flip_flop_2_qp), .Q(IDEX_BEQ));
  d_flip_flop d_flip_flop_3 (.Clr(Clr), .Clk(Clk), .d(Bne), .QP(d_flip_flop_3_qp), .Q(IDEX_BNE));
  d_flip_flop d_flip_flop_4 (.Clr(Clr), .Clk(Clk), .d(Alusrc), .QP(d_flip_flop_4_qp), .Q(IDEX_ALUSRC));
  d_flip_flop d_flip_flop_5 (.Clr(Clr), .Clk(Clk), .d(Regwrite), .QP(d_flip_flop_5_qp), .Q(IDEX_REGWRITE));
  d_flip_flop d_flip_flop_6 (.Clr(Clr), .Clk(Clk), .d(MemWrite), .QP(d_flip_flop_6_qp), .Q(IDEX_MEMWRITE));
  // NoConnect on d_flip_flop_1_qp
  // NoConnect on d_flip_flop_2_qp
  // NoConnect on d_flip_flop_3_qp
  // NoConnect on d_flip_flop_4_qp
  // NoConnect on d_flip_flop_5_qp
  // NoConnect on d_flip_flop_6_qp
endmodule

module ctrl_idex_4b (
  input  [3:0] Op,
  output REGDST,
  output ALUSRC,
  output MEMTOREG,
  output REGWRITE,
  output MEMWRITE,
  output BEQ,
  output BNE,
  output [2:0] ALUCTL
);

  wire dec_4x16_1b_1_egt, dec_4x16_1b_1_ffn, dec_4x16_1b_1_ftn, dec_4x16_1b_1_fur, dec_4x16_1b_1_fve,
       dec_4x16_1b_1_one, dec_4x16_1b_1_six, dec_4x16_1b_1_svn, dec_4x16_1b_1_thr, dec_4x16_1b_1_ttn,
       dec_4x16_1b_1_two, dec_4x16_1b_1_zro;

  dec_4x16_1b dec_4x16_1b_1 (
    .Op(Op), .ZRO(dec_4x16_1b_1_zro), .ONE(dec_4x16_1b_1_one), .TWO(dec_4x16_1b_1_two),
    .THR(dec_4x16_1b_1_thr), .FUR(dec_4x16_1b_1_fur), .FVE(dec_4x16_1b_1_fve), .SIX(dec_4x16_1b_1_six),
    .SVN(dec_4x16_1b_1_svn), .EGT(dec_4x16_1b_1_egt), .NIN(MEMTOREG), .TEN(MEMWRITE), .EVN(BEQ), .TWL(BNE),
    .TTN(dec_4x16_1b_1_ttn), .FTN(dec_4x16_1b_1_ftn), .FFN(dec_4x16_1b_1_ffn));
  // NoConnect on dec_4x16_1b_1_egt
  // NoConnect on dec_4x16_1b_1_ttn
  // NoConnect on dec_4x16_1b_1_ftn
  // NoConnect on dec_4x16_1b_1_ffn
  or or_1 (REGDST, dec_4x16_1b_1_zro, dec_4x16_1b_1_one, dec_4x16_1b_1_two, dec_4x16_1b_1_thr, dec_4x16_1b_1_fur);
  or or_2 (ALUSRC, dec_4x16_1b_1_fve, dec_4x16_1b_1_six, dec_4x16_1b_1_svn, MEMTOREG, MEMWRITE);
  NotExactlyOne xnor_1 (.out(REGWRITE), .in0(MEMWRITE), .in1(BEQ), .in2(BNE));
  or or_3 (ALUCTL[2], dec_4x16_1b_1_one, dec_4x16_1b_1_fur, dec_4x16_1b_1_six, BEQ, BNE);
  or or_4 (ALUCTL[0], dec_4x16_1b_1_thr, dec_4x16_1b_1_fur, dec_4x16_1b_1_six);
  NotExactlyOne xnor_2 (.out(ALUCTL[1]), .in0(dec_4x16_1b_1_two), .in1(dec_4x16_1b_1_thr), .in2(dec_4x16_1b_1_svn));
endmodule

// 2x1 MUX
module mux_2x1_1b (
  input  I0,
  input  I1,
  input  Op,
  output O
);

  wire and_1_out, and_2_out;

  and and_1 (and_1_out, I0, ~Op);  // AND_Gate
  and and_2 (and_2_out, I1, Op);
  or or_1 (O, and_1_out, and_2_out);
endmodule

// 2x1 MUX
module mux_2x1_2b (
  input  [1:0] I0,
  input  Op,
  input  [1:0] I1,
  output [1:0] O
);

  mux_2x1_1b mux_2x1_1b_1 (.I1(I1[0]), .I0(I0[0]), .Op(Op), .O(O[0]));
  mux_2x1_1b mux_2x1_1b_2 (.I1(I1[1]), .I0(I0[1]), .Op(Op), .O(O[1]));
endmodule

// 2x1 MUX
module mux_2x1_4b (
  input  [3:0] I0,
  input  Op,
  input  [3:0] I1,
  output [3:0] O
);

  mux_2x1_1b mux_2x1_1b_1 (.I1(I1[0]), .I0(I0[0]), .Op(Op), .O(O[0]));
  mux_2x1_1b mux_2x1_1b_2 (.I1(I1[1]), .I0(I0[1]), .Op(Op), .O(O[1]));
  mux_2x1_1b mux_2x1_1b_3 (.I1(I1[2]), .I0(I0[2]), .Op(Op), .O(O[2]));
  mux_2x1_1b mux_2x1_1b_4 (.I1(I1[3]), .I0(I0[3]), .Op(Op), .O(O[3]));
endmodule

// 2x1 MUX
module mux_2x1_16b (
  input  [15:0] I0,
  input  Op,
  input  [15:0] I1,
  output [15:0] O
);

  mux_2x1_4b mux_2x1_4b_1 (.I0(I0[3:0]), .I1(I1[3:0]), .Op(Op), .O(O[3:0]));
  mux_2x1_4b mux_2x1_4b_2 (.I0(I0[7:4]), .I1(I1[7:4]), .Op(Op), .O(O[7:4]));
  mux_2x1_4b mux_2x1_4b_3 (.I0(I0[11:8]), .I1(I1[11:8]), .Op(Op), .O(O[11:8]));
  mux_2x1_4b mux_2x1_4b_4 (.I0(I0[15:12]), .I1(I1[15:12]), .Op(Op), .O(O[15:12]));
endmodule

// 4x1 MUX
module mux_4x1_1b (
  input  I0,
  input  I1,
  input  I2,
  input  I3,
  input  [1:0] Op,
  output O
);

  wire mux_2x1_1b_1_o, mux_2x1_1b_2_o;

  mux_2x1_1b mux_2x1_1b_1 (.I1(I1), .I0(I0), .Op(Op[0]), .O(mux_2x1_1b_1_o));
  mux_2x1_1b mux_2x1_1b_2 (.I1(I3), .I0(I2), .Op(Op[0]), .O(mux_2x1_1b_2_o));
  mux_2x1_1b mux_2x1_1b_3 (.I1(mux_2x1_1b_2_o), .I0(mux_2x1_1b_1_o), .Op(Op[1]), .O(O));
endmodule

module mux_8x1_1b (
  input  I0,
  input  I1,
  input  I2,
  input  I3,
  input  I4,
  input  I5,
  input  I6,
  input  I7,
  input  [2:0] Op,
  output O
);

  wire mux_4x1_1b_1_o, mux_4x1_1b_2_o;

  mux_4x1_1b mux_4x1_1b_1 (.I0(I0), .I1(I1), .I2(I2), .I3(I3), .O(mux_4x1_1b_1_o));  // open: Op
  mux_4x1_1b mux_4x1_1b_2 (.I0(I4), .I1(I5), .I2(I6), .I3(I7), .O(mux_4x1_1b_2_o));  // open: Op
  mux_2x1_1b mux_2x1_1b_1 (.I1(mux_4x1_1b_2_o), .I0(mux_4x1_1b_1_o), .O(O));  // open: Op
endmodule

// 4x1 MUX
module mux_4x1_16b (
  input  [15:0] I0,
  input  [15:0] I1,
  input  [15:0] I2,
  input  [15:0] I3,
  input  [1:0] Op,
  output [15:0] O
);

  wire [15:0] mux_2x1_16b_1_o, mux_2x1_16b_2_o;

  mux_2x1_16b mux_2x1_16b_1 (.I0(I0), .I1(I1), .Op(Op[0]), .O(mux_2x1_16b_1_o));
  mux_2x1_16b mux_2x1_16b_2 (.I0(I2), .I1(I3), .Op(Op[0]), .O(mux_2x1_16b_2_o));
  mux_2x1_16b mux_2x1_16b_3 (.I0(mux_2x1_16b_1_o), .I1(mux_2x1_16b_2_o), .Op(Op[1]), .O(O));
endmodule

// 2x4 DEC
module dec_2x4_1b (
  input  [1:0] i,
  output O0,
  output O1,
  output O2,
  output O3
);

  and and_1 (O0, ~i[0], ~i[1]);  // AND_Gate
  and and_2 (O1, i[0], ~i[1]);  // AND_Gate
  and and_3 (O2, ~i[0], i[1]);  // AND_Gate
  and and_4 (O3, i[0], i[1]);
endmodule

// 4x16 DEC
module dec_4x16_1b (
  input  [3:0] Op,
  output ZRO,
  output EGT,
  output ONE,
  output NIN,
  output TWO,
  output TEN,
  output THR,
  output EVN,
  output FUR,
  output TWL,
  output FVE,
  output TTN,
  output SIX,
  output FTN,
  output SVN,
  output FFN
);

  and i_0 (ZRO, ~Op[0], ~Op[1], ~Op[2], ~Op[3]);  // AND_Gate
  and i_1 (ONE, Op[0], ~Op[1], ~Op[2], ~Op[3]);  // AND_Gate
  and i_2 (TWO, ~Op[0], Op[1], ~Op[2], ~Op[3]);  // AND_Gate
  and i_3 (THR, Op[0], Op[1], ~Op[2], ~Op[3]);  // AND_Gate
  and i_4 (FUR, ~Op[0], ~Op[1], Op[2], ~Op[3]);  // AND_Gate
  and i_5 (FVE, Op[0], ~Op[1], Op[2], ~Op[3]);  // AND_Gate
  and i_6 (SIX, ~Op[0], Op[1], Op[2], ~Op[3]);  // AND_Gate
  and i_7 (SVN, Op[0], Op[1], Op[2], ~Op[3]);  // AND_Gate
  and i_8 (EGT, ~Op[0], ~Op[1], ~Op[2], Op[3]);  // AND_Gate
  and i_9 (NIN, Op[0], ~Op[1], ~Op[2], Op[3]);  // AND_Gate
  and i_10 (TEN, ~Op[0], Op[1], ~Op[2], Op[3]);  // AND_Gate
  and i_11 (EVN, Op[0], Op[1], ~Op[2], Op[3]);  // AND_Gate
  and i_12 (TWL, ~Op[0], ~Op[1], Op[2], Op[3]);  // AND_Gate
  and i_13 (TTN, Op[0], ~Op[1], Op[2], Op[3]);  // AND_Gate
  and i_14 (FTN, ~Op[0], Op[1], Op[2], Op[3]);  // AND_Gate
  and i_15 (FFN, Op[0], Op[1], Op[2], Op[3]);
endmodule

// D LATCH
module d_latch (
  input  d,
  input  Clk,
  input  Clr,
  output Q,
  output QP
);

  wire a1_out, na1_out, na2_out;

  nand na2 (na2_out, Clk, ~d);  // NAND_Gate
  nand na1 (na1_out, d, Clk);
  and a1 (a1_out, na2_out, ~Clr);  // AND_Gate
  nand na3 (Q, na1_out, QP);
  nand na4 (QP, Q, a1_out);
endmodule

// D FLIP
module d_flip_flop (
  input  d,
  input  Clr,
  input  Clk,
  output Q,
  output QP
);

  wire dl1_q, dl1_qp, not_1_out;

  d_latch dl1 (.Clk(Clk), .Clr(Clr), .d(d), .QP(dl1_qp), .Q(dl1_q));
  // NoConnect on dl1_qp
  not not_1 (not_1_out, Clk);
  d_latch dl2 (.Clk(not_1_out), .Clr(Clr), .d(dl1_q), .QP(QP), .Q(Q));
endmodule

// D LOAD
module d_load_flop (
  input  Rin,
  input  Right,
  input  Lin,
  input  Load,
  input  Clr,
  input  Clk,
  output Q,
  output Q_p
);

  wire and_1_out, and_2_out, or_1_out, or_2_out;

  and and_1 (and_1_out, Rin, Right);
  and and_2 (and_2_out, ~Right, Lin);  // AND_Gate
  or or_1 (or_1_out, and_1_out, and_2_out);
  or or_2 (or_2_out, or_1_out, Load);
  d_flip_flop d_flip_flop_1 (.Clr(Clr), .Clk(Clk), .d(or_2_out), .QP(Q_p), .Q(Q));

  // Notes on the sheet:
  //   This is the basis for shift registers.
endmodule

// HALF ADDER
module half_adder (
  input  x,
  input  y,
  output S,
  output C
);

  wire nand_1_out, nand_2_out;

  nand nand_1 (nand_1_out, x, ~y);  // NAND_Gate
  nand nand_2 (nand_2_out, ~x, y);  // NAND_Gate
  nand nand_3 (S, nand_1_out, nand_2_out);
  and and_1 (C, x, y);
endmodule

// FULL ADDER
module full_adder (
  input  x,
  input  y,
  input  Cin,
  output S,
  output COUT
);

  wire half_adder_1_c, half_adder_1_s, half_adder_2_c;

  half_adder half_adder_1 (.y(y), .x(x), .C(half_adder_1_c), .S(half_adder_1_s));
  half_adder half_adder_2 (.y(Cin), .x(half_adder_1_s), .C(half_adder_2_c), .S(S));
  or or_1 (COUT, half_adder_2_c, half_adder_1_c);
endmodule

// REG 2B
module reg_2b (
  input  Clr,
  input  Clk,
  input  [1:0] d,
  output [1:0] Q
);

  wire d_flip_flop_2_qp;

  d_flip_flop d_flip_flop_1 (.Clr(Clr), .Clk(Clk), .d(d[0]), .Q(Q[0]));  // open: QP
  d_flip_flop d_flip_flop_2 (.Clr(Clr), .Clk(Clk), .d(d[1]), .QP(d_flip_flop_2_qp), .Q(Q[1]));
  // NoConnect on d_flip_flop_2_qp
endmodule

// REG 3B
module reg_3b (
  input  Clr,
  input  Clk,
  input  [2:0] d,
  output [2:0] Q
);

  wire d_flip_flop_1_qp, d_flip_flop_2_qp, d_flip_flop_3_qp;

  d_flip_flop d_flip_flop_1 (.Clr(Clr), .Clk(Clk), .d(d[0]), .QP(d_flip_flop_1_qp), .Q(Q[0]));
  d_flip_flop d_flip_flop_2 (.Clr(Clr), .Clk(Clk), .d(d[1]), .QP(d_flip_flop_2_qp), .Q(Q[1]));
  d_flip_flop d_flip_flop_3 (.Clr(Clr), .Clk(Clk), .d(d[2]), .QP(d_flip_flop_3_qp), .Q(Q[2]));
  // NoConnect on d_flip_flop_1_qp
  // NoConnect on d_flip_flop_2_qp
  // NoConnect on d_flip_flop_3_qp
endmodule

// REG 4B
module reg_4b (
  input  Clr,
  input  Clk,
  input  [3:0] d,
  output [3:0] Q
);

  wire d_flip_flop_1_qp, d_flip_flop_2_qp, d_flip_flop_3_qp, d_flip_flop_4_qp;

  d_flip_flop d_flip_flop_1 (.Clr(Clr), .Clk(Clk), .d(d[0]), .QP(d_flip_flop_1_qp), .Q(Q[0]));
  d_flip_flop d_flip_flop_2 (.Clr(Clr), .Clk(Clk), .d(d[1]), .QP(d_flip_flop_2_qp), .Q(Q[1]));
  d_flip_flop d_flip_flop_3 (.Clr(Clr), .Clk(Clk), .d(d[2]), .QP(d_flip_flop_3_qp), .Q(Q[2]));
  d_flip_flop d_flip_flop_4 (.Clr(Clr), .Clk(Clk), .d(d[3]), .QP(d_flip_flop_4_qp), .Q(Q[3]));
  // NoConnect on d_flip_flop_1_qp
  // NoConnect on d_flip_flop_2_qp
  // NoConnect on d_flip_flop_3_qp
  // NoConnect on d_flip_flop_4_qp
endmodule

// REG 16B
module reg_16b (
  input  Clr,
  input  Clk,
  input  [15:0] d,
  output [15:0] Q
);

  reg_4b reg_4b_1 (.d(d[3:0]), .Clr(Clr), .Clk(Clk), .Q(Q[3:0]));
  reg_4b reg_4b_2 (.d(d[7:4]), .Clr(Clr), .Clk(Clk), .Q(Q[7:4]));
  reg_4b reg_4b_3 (.d(d[11:8]), .Clr(Clr), .Clk(Clk), .Q(Q[11:8]));
  reg_4b reg_4b_4 (.d(d[15:12]), .Clr(Clr), .Clk(Clk), .Q(Q[15:12]));
endmodule

// FILE 16B
module regfile_4x_16b (
  input  [1:0] Rreg1,
  input  Clr,
  input  Clk,
  input  RegWrite,
  input  [1:0] Rreg2,
  input  [1:0] Wreg,
  input  [15:0] d,
  output [15:0] REG1,
  output [15:0] REG2
);

  wire and_1_out, and_2_out, and_3_out, dec_2x4_1b_1_o0, dec_2x4_1b_1_o1, dec_2x4_1b_1_o2, dec_2x4_1b_1_o3,
       undriven_2;
  wire [15:0] reg_16b_1_q, reg_16b_2_q, reg_16b_3_q, undriven, zero_reg_q;

  dec_2x4_1b dec_2x4_1b_1 (
    .i(Wreg), .O1(dec_2x4_1b_1_o1), .O2(dec_2x4_1b_1_o2), .O3(dec_2x4_1b_1_o3), .O0(dec_2x4_1b_1_o0));
  // NoConnect on dec_2x4_1b_1_o0
  and and_1 (and_1_out, RegWrite, dec_2x4_1b_1_o1, Clk);
  and and_2 (and_2_out, RegWrite, dec_2x4_1b_1_o2, Clk);
  and and_3 (and_3_out, RegWrite, dec_2x4_1b_1_o3, Clk);
  reg_16b zero_reg (.Clk(undriven_2), .Clr(1'b1), .d(undriven), .Q(zero_reg_q));
  // NoConnect on undriven
  // NoConnect on undriven_2
  reg_16b reg_16b_1 (.Clk(and_1_out), .Clr(Clr), .d(d), .Q(reg_16b_1_q));
  reg_16b reg_16b_2 (.Clk(and_2_out), .Clr(Clr), .d(d), .Q(reg_16b_2_q));
  reg_16b reg_16b_3 (.Clk(and_3_out), .Clr(Clr), .d(d), .Q(reg_16b_3_q));
  mux_4x1_16b mux_4x1_16b_1 (
    .I1(reg_16b_1_q), .I2(reg_16b_2_q), .I3(reg_16b_3_q), .I0(zero_reg_q), .Op(Rreg1), .O(REG1));
  mux_4x1_16b mux_4x1_16b_2 (
    .I1(reg_16b_1_q), .I2(reg_16b_2_q), .I3(reg_16b_3_q), .I0(zero_reg_q), .Op(Rreg2), .O(REG2));
endmodule

// ALU 1B
module alu_1b (
  input  [2:0] Op,
  input  x,
  input  y,
  input  Less,
  input  Cin,
  output R,
  output SET,
  output COUT,
  output O
);

  wire and_1_out, full_adder_1_cout, or_1_out, xor_1_out, xor_2_out;

  xor xor_1 (xor_1_out, y, Op[2]);
  full_adder full_adder_1 (.y(xor_1_out), .Cin(Cin), .x(x), .S(SET), .COUT(full_adder_1_cout));
  and and_1 (and_1_out, x, xor_1_out);
  or or_1 (or_1_out, x, xor_1_out);
  xor xor_2 (xor_2_out, Cin, full_adder_1_cout);
  mux_4x1_1b mux_4x1_1b_1 (.I0(and_1_out), .I1(or_1_out), .I2(SET), .I3(Less), .Op(Op[1:0]), .O(R));
  and and_2 (COUT, Op[1], full_adder_1_cout);
  and and_3 (O, Op[1], xor_2_out);
endmodule

module alu_1b_4bop (
  input  [3:0] Op,
  input  x,
  input  y,
  input  Less,
  input  Cin,
  output R,
  output SET,
  output COUT,
  output O
);

  wire and_1_out, full_adder_1_cout, or_1_out, xor_1_out, xor_2_out, xor_3_out;

  xor xor_1 (xor_1_out, x, Op[3]);
  xor xor_2 (xor_2_out, y, Op[2]);
  full_adder full_adder_1 (.y(xor_2_out), .Cin(Cin), .x(xor_1_out), .S(SET), .COUT(full_adder_1_cout));
  and and_1 (and_1_out, xor_1_out, xor_2_out);
  or or_1 (or_1_out, xor_1_out, xor_2_out);
  xor xor_3 (xor_3_out, Cin, full_adder_1_cout);
  mux_4x1_1b mux_4x1_1b_1 (.I0(and_1_out), .I1(or_1_out), .I2(SET), .I3(Less), .Op(Op[1:0]), .O(R));
  and and_2 (COUT, Op[1], full_adder_1_cout);
  and and_3 (O, Op[1], xor_3_out);
endmodule

// ALU 4B O
module alu_4b_open (
  input  [3:0] x,
  input  [2:0] Op,
  input  Less,
  input  Cin,
  input  [3:0] y,
  output [3:0] R,
  output ZERO,
  output O,
  output SET,
  output COUT
);

  wire alu_1b_1_cout, alu_1b_1_o, alu_1b_1_set, alu_1b_2_cout, alu_1b_2_o, alu_1b_2_set, alu_1b_3_cout,
       alu_1b_3_o, alu_1b_3_set;

  alu_1b alu_1b_1 (
    .Op(Op), .y(y[0]), .Less(Less), .Cin(Cin), .x(x[0]), .R(R[0]), .SET(alu_1b_1_set), .COUT(alu_1b_1_cout),
    .O(alu_1b_1_o));
  alu_1b alu_1b_2 (
    .Op(Op), .y(y[1]), .Less(1'b0), .Cin(alu_1b_1_cout), .x(x[1]), .R(R[1]), .SET(alu_1b_2_set),
    .COUT(alu_1b_2_cout), .O(alu_1b_2_o));
  alu_1b alu_1b_3 (
    .Op(Op), .y(y[2]), .Less(1'b0), .Cin(alu_1b_2_cout), .x(x[2]), .R(R[2]), .SET(alu_1b_3_set),
    .COUT(alu_1b_3_cout), .O(alu_1b_3_o));
  alu_1b alu_1b_4 (
    .Op(Op), .y(y[3]), .Less(1'b0), .Cin(alu_1b_3_cout), .x(x[3]), .R(R[3]), .SET(SET), .COUT(COUT), .O(O));
  // NoConnect on alu_1b_1_o
  // NoConnect on alu_1b_1_set
  // NoConnect on alu_1b_2_o
  // NoConnect on alu_1b_2_set
  // NoConnect on alu_1b_3_o
  // NoConnect on alu_1b_3_set
  and and_1 (ZERO, ~R[0], ~R[1], ~R[2], ~R[3]);  // AND_Gate
endmodule

// ALU 4B
module alu_4b (
  input  [2:0] Op,
  input  [3:0] x,
  input  [3:0] y,
  output [3:0] R,
  output O,
  output ZERO
);

  wire alu_4b_open_1_cout, alu_4b_open_1_set;

  alu_4b_open alu_4b_open_1 (
    .Less(alu_4b_open_1_set), .Cin(Op[2]), .x(x), .y(y), .Op(Op), .O(O), .SET(alu_4b_open_1_set),
    .COUT(alu_4b_open_1_cout), .R(R), .ZERO(ZERO));
  // NoConnect on alu_4b_open_1_cout
endmodule

// ALU 16B O
module alu_16b_open (
  input  [15:0] x,
  input  [2:0] Op,
  input  Less,
  input  Cin,
  input  [15:0] y,
  output [15:0] R,
  output ZERO,
  output O,
  output SET,
  output COUT
);

  wire alu_4b_open_1_cout, alu_4b_open_1_o, alu_4b_open_1_set, alu_4b_open_1_zero, alu_4b_open_2_cout,
       alu_4b_open_2_o, alu_4b_open_2_set, alu_4b_open_2_zero, alu_4b_open_3_cout, alu_4b_open_3_o,
       alu_4b_open_3_set, alu_4b_open_3_zero, alu_4b_open_4_zero;

  alu_4b_open alu_4b_open_1 (
    .Less(Less), .Cin(Cin), .x(x[3:0]), .y(y[3:0]), .Op(Op), .O(alu_4b_open_1_o), .SET(alu_4b_open_1_set),
    .COUT(alu_4b_open_1_cout), .R(R[3:0]), .ZERO(alu_4b_open_1_zero));
  alu_4b_open alu_4b_open_2 (
    .Less(1'b0), .Cin(alu_4b_open_1_cout), .x(x[7:4]), .y(y[7:4]), .Op(Op), .O(alu_4b_open_2_o),
    .SET(alu_4b_open_2_set), .COUT(alu_4b_open_2_cout), .R(R[7:4]), .ZERO(alu_4b_open_2_zero));
  alu_4b_open alu_4b_open_3 (
    .Less(1'b0), .Cin(alu_4b_open_2_cout), .x(x[11:8]), .y(y[11:8]), .Op(Op), .O(alu_4b_open_3_o),
    .SET(alu_4b_open_3_set), .COUT(alu_4b_open_3_cout), .R(R[11:8]), .ZERO(alu_4b_open_3_zero));
  alu_4b_open alu_4b_open_4 (
    .Less(1'b0), .Cin(alu_4b_open_3_cout), .x(x[15:12]), .y(y[15:12]), .Op(Op), .O(O), .SET(SET),
    .COUT(COUT), .R(R[15:12]), .ZERO(alu_4b_open_4_zero));
  // NoConnect on alu_4b_open_1_o
  // NoConnect on alu_4b_open_1_set
  // NoConnect on alu_4b_open_2_o
  // NoConnect on alu_4b_open_2_set
  // NoConnect on alu_4b_open_3_o
  // NoConnect on alu_4b_open_3_set
  and and_1 (ZERO, alu_4b_open_1_zero, alu_4b_open_2_zero, alu_4b_open_3_zero, alu_4b_open_4_zero);
endmodule

// ALU 16B
module alu_16b (
  input  [15:0] x,
  input  [2:0] Op,
  input  [15:0] y,
  output [15:0] R,
  output ZERO,
  output O
);

  wire alu_4b_open_1_cout, alu_4b_open_1_o, alu_4b_open_1_set, alu_4b_open_1_zero, alu_4b_open_2_cout,
       alu_4b_open_2_o, alu_4b_open_2_set, alu_4b_open_2_zero, alu_4b_open_3_cout, alu_4b_open_3_o,
       alu_4b_open_3_set, alu_4b_open_3_zero, alu_4b_open_4_cout, alu_4b_open_4_set, alu_4b_open_4_zero;

  alu_4b_open alu_4b_open_1 (
    .Less(alu_4b_open_4_set), .Cin(1'b0), .x(x[3:0]), .y(y[3:0]), .Op(Op), .O(alu_4b_open_1_o),
    .SET(alu_4b_open_1_set), .COUT(alu_4b_open_1_cout), .R(R[3:0]), .ZERO(alu_4b_open_1_zero));
  alu_4b_open alu_4b_open_2 (
    .Less(1'b0), .Cin(alu_4b_open_1_cout), .x(x[7:4]), .y(y[7:4]), .Op(Op), .O(alu_4b_open_2_o),
    .SET(alu_4b_open_2_set), .COUT(alu_4b_open_2_cout), .R(R[7:4]), .ZERO(alu_4b_open_2_zero));
  alu_4b_open alu_4b_open_3 (
    .Less(1'b0), .Cin(alu_4b_open_2_cout), .x(x[11:8]), .y(y[11:8]), .Op(Op), .O(alu_4b_open_3_o),
    .SET(alu_4b_open_3_set), .COUT(alu_4b_open_3_cout), .R(R[11:8]), .ZERO(alu_4b_open_3_zero));
  alu_4b_open alu_4b_open_4 (
    .Less(1'b0), .Cin(alu_4b_open_3_cout), .x(x[15:12]), .y(y[15:12]), .Op(Op), .O(O),
    .SET(alu_4b_open_4_set), .COUT(alu_4b_open_4_cout), .R(R[15:12]), .ZERO(alu_4b_open_4_zero));
  // NoConnect on alu_4b_open_1_o
  // NoConnect on alu_4b_open_1_set
  // NoConnect on alu_4b_open_2_o
  // NoConnect on alu_4b_open_2_set
  // NoConnect on alu_4b_open_3_o
  // NoConnect on alu_4b_open_3_set
  // NoConnect on alu_4b_open_4_cout
  and and_1 (ZERO, alu_4b_open_1_zero, alu_4b_open_2_zero, alu_4b_open_3_zero, alu_4b_open_4_zero);
endmodule

// SHFT 4B
module shft_1_4b (
  input  [3:0] Load,
  input  Right,
  input  Sl,
  input  Sr,
  input  Clk,
  input  Clr,
  output SLEFT,
  output SRIGHT,
  output [3:0] Q
);

  wire d_load_flop_1_q_p, d_load_flop_2_q_p, d_load_flop_3_q_p, d_load_flop_4_q_p;

  d_load_flop d_load_flop_1 (
    .Right(Right), .Lin(Sl), .Load(Load[0]), .Clr(Clr), .Clk(Clk), .Rin(Q[1]), .Q(Q[0]),
    .Q_p(d_load_flop_1_q_p));
  d_load_flop d_load_flop_2 (
    .Right(Right), .Lin(Q[0]), .Load(Load[1]), .Clr(Clr), .Clk(Clk), .Rin(Q[2]), .Q(Q[1]),
    .Q_p(d_load_flop_2_q_p));
  // NoConnect on d_load_flop_1_q_p
  // Probe on Load
  // NoConnect on d_load_flop_2_q_p
  d_load_flop d_load_flop_3 (
    .Right(Right), .Lin(Q[1]), .Load(Load[2]), .Clr(Clr), .Clk(Clk), .Rin(Q[3]), .Q(Q[2]),
    .Q_p(d_load_flop_3_q_p));
  // Probe on Q
  // NoConnect on d_load_flop_3_q_p
  d_load_flop d_load_flop_4 (
    .Right(Right), .Lin(Q[2]), .Load(Load[3]), .Clr(Clr), .Clk(Clk), .Rin(Sr), .Q(Q[3]),
    .Q_p(d_load_flop_4_q_p));
  // NoConnect on d_load_flop_4_q_p

  assign SLEFT = Q[0];
  assign SRIGHT = Q[3];
endmodule

module shft_1_16b (
  input  Clr,
  input  Right,
  input  Clk,
  input  [15:0] Load,
  output [15:0] Q
);

  wire shft_1_4b_1_sright, shft_1_4b_2_sleft, shft_1_4b_2_sright, shft_1_4b_3_sleft, shft_1_4b_3_sright,
       shft_1_4b_4_sleft;

  shft_1_4b shft_1_4b_1 (
    .Clr(Clr), .Clk(Clk), .Right(Right), .Load(Load[3:0]), .Sr(shft_1_4b_2_sleft), .Q(Q[3:0]),
    .SRIGHT(shft_1_4b_1_sright));  // open: Sl, SLEFT
  shft_1_4b shft_1_4b_2 (
    .Sl(shft_1_4b_1_sright), .Clr(Clr), .Clk(Clk), .Right(Right), .Load(Load[7:4]), .Sr(shft_1_4b_3_sleft),
    .SLEFT(shft_1_4b_2_sleft), .Q(Q[7:4]), .SRIGHT(shft_1_4b_2_sright));
  shft_1_4b shft_1_4b_3 (
    .Sl(shft_1_4b_2_sright), .Clr(Clr), .Clk(Clk), .Right(Right), .Load(Load[11:8]), .Sr(shft_1_4b_4_sleft),
    .SLEFT(shft_1_4b_3_sleft), .Q(Q[11:8]), .SRIGHT(shft_1_4b_3_sright));
  shft_1_4b shft_1_4b_4 (
    .Sl(shft_1_4b_3_sright), .Clr(Clr), .Clk(Clk), .Right(Right), .Load(Load[15:12]),
    .SLEFT(shft_1_4b_4_sleft), .Q(Q[15:12]));  // open: Sr, SRIGHT
endmodule

module tcomp_3b (
  input  [2:0] in_1,
  output [2:0] out_2
);

  wire half_adder_1_c, half_adder_2_c, half_adder_3_c, not_1_out, not_2_out, not_3_out;

  half_adder half_adder_1 (.y(1'b1), .x(not_1_out), .C(half_adder_1_c), .S(out_2[0]));
  not not_1 (not_1_out, in_1[0]);
  half_adder half_adder_2 (.y(half_adder_1_c), .x(not_2_out), .C(half_adder_2_c), .S(out_2[1]));
  not not_2 (not_2_out, in_1[1]);
  half_adder half_adder_3 (.y(half_adder_2_c), .x(not_3_out), .C(half_adder_3_c), .S(out_2[2]));
  not not_3 (not_3_out, in_1[2]);
  // NoConnect on half_adder_3_c
endmodule
